# Fritzing sketch FireFighterPrint (saved by Fritzing 0.9.2b)
breadboards: 1

parts:
  Componente1 = Arduino Uno (Rev3)
  J1 = Basic Servo
  J2 = Basic Servo
  S1 = Pushbutton [package="[THT]"]
  R1 = Resistor [tolerance=±5% resistance=220 package=THT]
  Componente2 = Thumb Joystick
  IC1 = Voltage Regulator LM1117 [package=sot223]
  M1 = DC Motor

nets:
  N1: Componente1.A0, Componente2.VERT
  N2: Componente1.A1, Componente2.HORZ
  VCC: Componente1.D2, J1.vcc, J2.vcc, S1.Pin_3, S1.Pin_4, Componente2.VCC
  N3: Componente1.D3_PWM, J2.pulse
  N4: Componente1.D4, J1.pulse
  GND: J1.gnd, J2.gnd, R1.Pin_0, Componente2.GND, IC1.IN
  N5: S1.Pin_1, S1.Pin_2, R1.Pin_1, IC1.OUT, M1.pin_2
  N6: IC1.ADJ, M1.pin_1
