# Fritzing sketch ElevadorPrint (saved by Fritzing 0.9.2b)
breadboards: 1

parts:
  U2 = 7-SEGMENT-DISPLAY [package=7-segment-display]
  R1 = Resistor [tolerance=±5% resistance=220 package=THT]
  R2 = Resistor [tolerance=±5% resistance=220 package=THT]
  R3 = Resistor [tolerance=±5% resistance=220 package=THT]
  R4 = Resistor [tolerance=±5% resistance=220 package=THT]
  R5 = Resistor [tolerance=±5% resistance=220 package=THT]
  R6 = Resistor [tolerance=±5% resistance=220 package=THT]
  Componente1 = Arduino Uno (Rev3)
  S1 = Pushbutton [package="[THT]"]
  S2 = Pushbutton [package="[THT]"]
  S3 = Pushbutton [package="[THT]"]
  R7 = Resistor [tolerance=±5% resistance=220 package=THT]
  R8 = Resistor [tolerance=±5% resistance=220 package=THT]
  R9 = Resistor [tolerance=±5% resistance=220 package=THT]
  IC2 = L293D [package=THT]
  M1 = DC Motor

nets:
  N1: U2.D, R1.Pin_0
  N2: U2.G1, R2.Pin_0
  N3: U2.C, U2.F, Componente1.5V, S1.Pin_1, S1.Pin_2, S2.Pin_1, S2.Pin_2, S3.Pin_1, S3.Pin_2, IC2.+Vmotor, IC2.+V
  N4: U2.DP, R3.Pin_0
  N5: U2.A, R4.Pin_1
  N6: U2.G2, R5.Pin_1
  N7: U2.G, R6.Pin_1
  N8: R1.Pin_1, Componente1.D2
  N9: R2.Pin_1, Componente1.D3_PWM
  N10: R3.Pin_1, Componente1.D4
  N11: R4.Pin_0, Componente1.D5_PWM
  N12: R5.Pin_0, Componente1.D6_PWM
  N13: R6.Pin_0, Componente1.D7
  N14: Componente1.D8, R7.Pin_1
  N15: Componente1.D9_PWM, R8.Pin_1
  N16: Componente1.D10_PWM/SS, R9.Pin_1
  N17: Componente1.D12/MISO, IC2.In_1
  N18: Componente1.D13/SCK, IC2.In_2
  N19: Componente1.GND, IC2.0V
  N20: S1.Pin_3, S1.Pin_4, R7.Pin_0
  N21: S2.Pin_3, S2.Pin_4, R8.Pin_0
  N22: S3.Pin_3, S3.Pin_4, R9.Pin_0
  N23: IC2.Out_1_(_Controlled_by_Enable_1_), M1.pin_1
  N24: IC2.Out_2_(_Controlled_by_Enable_1_), M1.pin_2
