# Fritzing sketch MathQuizPrint (saved by Fritzing 0.9.2b)
breadboards: 1

parts:
  Componente1 = Arduino Uno (Rev3)
  J1 = Basic Servo
  LED1 = LED - 5mm [color="Red (633nm)" package="5 mm [THT]"]
  LED2 = LED - 5mm [color="Red (633nm)" package="5 mm [THT]"]
  R1 = Resistor [tolerance=±5% resistance=220 package=THT]
  R2 = Resistor [tolerance=±5% resistance=220 package=THT]
  J2 = Piezo Speaker
  R3 = Resistor [tolerance=±5% resistance=220 package=THT]

nets:
  N1: Componente1.D2, J1.pulse
  N2: Componente1.D3_PWM, R1.Pin_0
  N3: Componente1.D4, R2.Pin_0
  N4: Componente1.D5_PWM, R3.Pin_0
  5V: Componente1.5V, J1.vcc
  GND: Componente1.GND, J1.gnd, LED1.cathode, LED2.cathode, J2.pin1
  N5: LED1.anode, R1.Pin_1
  N6: LED2.anode, R2.Pin_1
  N7: J2.pin2, R3.Pin_1
