# Fritzing sketch MorsePrint (saved by Fritzing 0.9.2b)
breadboards: 2

parts:
  Componente1 = Arduino Uno (Rev3)
  S1 = Pushbutton [package="[THT]"]
  LED1 = LED - 5mm [color="Red (633nm)" package="5 mm [THT]"]
  R1 = Resistor [tolerance=±5% resistance=220 package=THT]
  Componente2 = Arduino Uno (Rev3)
  LED2 = LED - 5mm [color="Red (633nm)" package="5 mm [THT]"]
  R2 = Resistor [tolerance=±5% resistance=220 package=THT]
  P1 = S1133 Si Photodiode [package="8mm Ceramic [THT]"]

nets:
  N1: Componente1.D2, R1.Pin_0
  N2: Componente1.D3_PWM, S1.Pin_3, S1.Pin_4
  N3: Componente1.GND, S1.Pin_1, S1.Pin_2, LED1.cathode
  N4: LED1.anode, R1.Pin_1
  N5: Componente2.D2, Componente2.D3_PWM, Componente2.D4, Componente2.5V, P1.anode
  N6: Componente2.GND, LED2.cathode, P1.cathode
  N7: LED2.anode, R2.Pin_0
