# Fritzing sketch ShoppingPrint (saved by Fritzing 0.9.2b)
breadboards: 1

parts:
  Componente1 = Arduino Uno (Rev3)
  J1 = Infrared Proximity Sensor
  LED1 = LED - 5mm [color="Red (633nm)" package="5 mm [THT]"]
  LED2 = LED - 5mm [color="Red (633nm)" package="5 mm [THT]"]
  R1 = Resistor [tolerance=±5% resistance=220 package=THT]
  R2 = Resistor [tolerance=±5% resistance=220 package=THT]
  J2 = Basic Servo
  Componente2 = SRF05 Ultrasonic Rangefinder

nets:
  N1: Componente1.A0, J1.Vout
  N2: Componente1.A1, Componente2.Echo
  N3: Componente1.D8, R1.Pin_0
  N4: Componente1.D9_PWM, R2.Pin_0
  N5: Componente1.D2, J2.pulse
  VCC: Componente1.5V, J1.Vcc, J2.vcc, Componente2.VCC
  GND: Componente1.GND, J1.GND, LED1.cathode, LED2.cathode, J2.gnd, Componente2.GND
  N6: LED1.anode, R1.Pin_1
  N7: LED2.anode, R2.Pin_1
